# Fritzing sketch LightningFlash (saved by Fritzing 1.0.2b)

parts:
  Digispark1 = Digispark  # not connected
  U1 = TerrainTronics Carew Castle
  LED1 = 1W LED with Resistor
  VCC1 = 4 x AAA Battery Mount

nets:
  N1: U1.+5V, VCC1.+
  N2: U1.GND1, LED1.cathode#2, VCC1.-
  N3: U1.LED+, LED1.anode#3

notes:
  Use a battery pack that has a switch. Remove batteries while programming over USB.
  This should be 3x batteries!
  This Star LED should have a built in resistor.
  This digispark is arduino IDE compatible. Flash Code available.

custom parts:
  Digispark: The Digispark is an Attiny85 based microcontroller development board similar to the Arduino line, only cheaper, smaller, and a bit less powerful. With a whole host of shields to extend its functionality and the ability to use the familiar Arduino IDE the Digispark is a great way to jump into electronics, or perfect for when an Arduino is too big or too much.
  1W LED with Resistor: Generic 1W 5V LED with integrated resistor.
